# Fritzing sketch infra1 (saved by Fritzing 0.9.0b)

parts:
  Parte1 = Arduino Mega 2560 (Rev3)
  J1 = Infrared Proximity Sensor

nets:
  N1: Parte1.D9_PWM, J1.Vout
  5V: Parte1.5V, J1.Vcc
  GND: Parte1.GND, J1.GND

notes:
  El primer programa del infrarrojo solo se tenia que observar los valores que nos regresaba despues de haberlos recibidos; asi como su funcionamiento
